# Fritzing sketch Weatherstation (saved by Fritzing 0.9.3b)
circuit board: 8.46667cm x 5.64444cm
breadboards: 1

parts:
  Pi_Pico = Raspberry Pi Pico H
  BME280 = BME280 Breakout
  NRF24 = NRF24L01+ Breakout Board
  R1 = Resistor [tolerance=±5% resistance=4.7k package=THT]
  Wind = RJ45 Jack [package=rj45-8]
  Rain = RJ45 Jack [package=rj45-8]

nets:
  N1: Pi_Pico.GP0, NRF24.CS
  N2: Pi_Pico.GP1, BME280.!CS
  GND: Pi_Pico.GND, BME280.GND, NRF24.GND, Wind.2
  N3: Pi_Pico.GP2, BME280.SCK/SCL, NRF24.SCK
  N4: Pi_Pico.GP3, BME280.SDI/SDA, NRF24.MOSI
  N5: Pi_Pico.GP4, BME280.SDO/ADR, NRF24.MISO
  N6: Pi_Pico.GP5, NRF24.CE
  N7: Pi_Pico.GP16, Rain.4
  N8: Pi_Pico.GP22, Wind.4
  N9: Pi_Pico.GP26, R1.Pin_1, Wind.5
  3.3V: Pi_Pico.3V3OUT, BME280.3.3V, NRF24.VCC, R1.Pin_0, Wind.3, Rain.3

custom parts:
  Raspberry Pi Pico H: Raspberry Pi Pico H. Based around the RP2040 microcontroller the Pico H is a low cost microcontroller device bringing Raspberry Pi quality, cost, and easy of use to the microcontroller space.
